# Fritzing sketch Phase1-led_buzzer (saved by Fritzing 1.0.1rc)
breadboards: 1

parts:
  Raspberry_Pi_1 = Raspberry Pi 3 [part_number=RPI-3-V1.2]  # not connected
  LED1 = smd LED [color="Red (633nm)" package="0603 [SMD]"]
  LED2 = smd LED [color="Blue (430nm)" package="0805 [SMD]"]
  SG2 = Buzzer 12mm [package=buzzer-12mm-ns]
  R1 = Resistor [tolerance=±5% power=0.25 resistance=220 package=THT]
  R2 = Resistor [tolerance=±5% power=0.25 resistance=220 package=THT]
  Part1 = Adafruit T-Cobbler Plus [part_number="Adafruit #1989 and #2028"]

nets:
  N1: LED1.cathode, SG2.2, R1.Pin_1, R2.Pin_0, Part1.GND
  N2: LED2.cathode, R1.Pin_0
  N3: LED2.anode, Part1.GPIO17
  N4: SG2.1, Part1.GPIO21

custom parts:
  Adafruit T-Cobbler Plus: The Raspberry Pi has landed on the Maker World like a 40-GPIO pinned, quad-USB ported, credit card sized bomb of DIY joy. And while you can use most of our great Model B accessories by hooking up our downgrade cable, its probably a good time to upgrade your set up and accessorize using all of the 40 pins. That's why we now carry the Assembled Adafruit Pi T-Cobbler Plus - Breakout + Cable for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
