# Fritzing sketch SmartStore_Phase2_ESP32_DHT11 (saved by Fritzing 1.0.1rc)
breadboards: 1

parts:
  MH-ET_LIVE_ESP32_DEVKIT1 = MH-ET LIVE ESP32 DEVKIT 38 pins
  DHT1 = DHT11 Humitidy and Temperature Sensor
  R1 = Resistor [tolerance=±5% resistance=10 package="0805 [SMD]"]
  MH-ET_LIVE_ESP32_DEVKIT2 = MH-ET LIVE ESP32 DEVKIT 38 pins
  DHT2 = DHT11 Humitidy and Temperature Sensor
  R2 = Resistor [tolerance=±5% resistance=10 package="0805 [SMD]"]

nets:
  3V3: MH-ET_LIVE_ESP32_DEVKIT1.3V3, DHT1.VDD, R1.Pin_0
  GND: MH-ET_LIVE_ESP32_DEVKIT1.GND, DHT1.GND
  N1: MH-ET_LIVE_ESP32_DEVKIT1.IO4, DHT1.DATA, R1.Pin_1
  3V3_2: MH-ET_LIVE_ESP32_DEVKIT2.3V3, DHT2.VDD, R2.Pin_0
  GND_2: MH-ET_LIVE_ESP32_DEVKIT2.GND, DHT2.GND
  N2: MH-ET_LIVE_ESP32_DEVKIT2.IO4, DHT2.DATA, R2.Pin_1

notes:
  Frig1
  Frig2

custom parts:
  MH-ET LIVE ESP32 DEVKIT 38 pins: http://mh.nodebb.com/topic/2/mh-et-live-esp32-devkit
  DHT11 Humitidy and Temperature Sensor: DHT11 Humidity and Temperature Sensor
